// Logisim project SINCRONOFFJK.circ as structural Verilog: 1 circuit, main circuit main
module main (
  output [2:0] out_1
);

  wire A_qn, and_1_out, clock_1_out, j_k_ff_2_qn, or_1_out, or_2_out;

  and and_1 (and_1_out, j_k_ff_2_qn, out_1[1]);
  Clock clock_1 (.out(clock_1_out));
  J_K_Flip_Flop A (
    .J(and_1_out), .clk(clock_1_out), .K(and_1_out), .Q(out_1[2]), .Qn(A_qn));  // open: preset, en, reset
  or or_1 (or_1_out, out_1[2], j_k_ff_2_qn);
  // Probe on out_1
  J_K_Flip_Flop j_k_ff_1 (.J(or_1_out), .clk(clock_1_out), .K(or_1_out), .Q(out_1[1]));  // open: Qn, preset, en, reset
  J_K_Flip_Flop j_k_ff_2 (
    .J(or_2_out), .clk(clock_1_out), .K(or_2_out), .Q(out_1[0]), .Qn(j_k_ff_2_qn));  // open: preset, en, reset
  or or_2 (or_2_out, out_1[1], A_qn);
endmodule
